# Fritzing sketch car_ver01 (saved by Fritzing 0.9.2b)
breadboards: 1

parts:
  Part1 = Arduino Uno (Rev3) [part_number="Genuino 101"]
  M1 = DC Motor  # not connected
  M2 = DC Motor  # not connected
  BAT1 = Battery Holders [package=battery-aa]
  BAT2 = Battery Holders [package=battery-aa]
  J1 = Infrared Proximity Sensor
  D1 = Zener Diode [part_number=1N4732A breakdown_voltage=3.6V package="300 mil [THT]"]  # not connected

nets:
  N1: Part1.A0, J1.Vout
  N2: Part1.GND, BAT1.-
  N3: BAT1.+, BAT2.-

notes:
  7.4 V
  3.7V
  5V
